// Logisim project OC.circ as structural Verilog: 16 circuits, main circuit main
module main (
  input  in_1,
  input  s,
  input  in_3,
  input  in_4,
  input  in_5,
  input  in_6,
  input  in_7,
  input  in_8,
  input  in_9,
  input  in_10,
  input  bus1,
  input  [2:0] OP,
  input  in_13,
  input  C_i,
  input  e,
  input  e_2,
  input  s_2,
  input  s_3,
  input  in_19,
  output C_o,
  output A_Maior,
  output Igual,
  output zero
);

  wire undriven;
  wire [7:0] bus1_1_out_3, controlled_buffer_1_out, MAR_q, ram_1_data, register_1_q, register_2_q,
       register_3_q, register_4_q, register_5_q, register_6_q, register_7_q, TMP_q, ula_1_result;

  ULA ula_1 (
    .A(controlled_buffer_1_out), .B(bus1_1_out_3), .Result(ula_1_result), .OP(OP), .Cin(C_i), .Cout(C_o),
    .A_Maior(A_Maior), .Igual(Igual), .Zero(zero));
  Register register_1 (.D(ula_1_result), .Q(register_1_q), .clk(s_2));  // open: en, clr
  Register TMP (.D(controlled_buffer_1_out), .Q(TMP_q), .clk(s));  // open: en, clr
  assign controlled_buffer_1_out = e ? register_1_q : 8'bz;  // Controlled_Buffer controlled_buffer_1
  // Probe on controlled_buffer_1_out
  bus1 bus1_1 (.in_1(TMP_q), .out_3(bus1_1_out_3), .in_2(bus1));
  assign controlled_buffer_1_out = in_8 ? register_2_q : 8'bz;  // Controlled_Buffer controlled_buffer_2
  Register register_2 (.D(controlled_buffer_1_out), .Q(register_2_q), .clk(in_7));  // open: en, clr
  assign controlled_buffer_1_out = in_4 ? register_3_q : 8'bz;  // Controlled_Buffer controlled_buffer_3
  Register register_3 (.D(controlled_buffer_1_out), .Q(register_3_q), .clk(in_3));  // open: en, clr
  Register register_4 (.D(controlled_buffer_1_out), .Q(register_4_q), .clk(s_3));  // open: en, clr
  assign controlled_buffer_1_out = e_2 ? register_4_q : 8'bz;  // Controlled_Buffer controlled_buffer_4
  assign controlled_buffer_1_out = in_10 ? register_5_q : 8'bz;  // Controlled_Buffer controlled_buffer_5
  Register register_5 (.D(controlled_buffer_1_out), .Q(register_5_q), .clk(in_9));  // open: en, clr
  Register register_6 (.D(controlled_buffer_1_out), .Q(register_6_q), .clk(in_19));  // open: en, clr
  assign controlled_buffer_1_out = in_6 ? register_7_q : 8'bz;  // Controlled_Buffer controlled_buffer_6
  Register register_7 (.D(controlled_buffer_1_out), .Q(register_7_q), .clk(in_5));  // open: en, clr
  Register MAR (.D(controlled_buffer_1_out), .Q(MAR_q), .clk(in_1));  // open: en, clr
  RAM #(.databus("bidir")) ram_1 (.addr(MAR_q), .we(undriven), .oe(in_13), .clk(in_13), .data(ram_1_data));
  // Probe on ram_1_data

  // Notes on the sheet:
  //   ACC
  //   000 | soma
  //   001 | S_Right
  //   010 | S_Left
  //   011 | Not
  //   100 | And
  //   101 | Or
  //   110 | Xor
  //   R0
  //   R1
  //   IAR
  //   R2
  //   WE = Write Enble
  //   OE = Output Enable
  //   Clock
  //   IR
  //   s
  //   R3
endmodule

module somador1bit (
  input  Cin,
  input  A,
  input  B,
  output S,
  output Cout
);

  wire and_1_out, and_2_out, xor_1_out;

  and and_1 (and_1_out, A, B);
  xor xor_1 (xor_1_out, A, B);
  or or_1 (Cout, and_1_out, and_2_out);
  and and_2 (and_2_out, xor_1_out, Cin);
  xor xor_2 (S, Cin, xor_1_out);
endmodule

module somador8bits (
  input  [7:0] A,
  input  in_2,
  input  [7:0] B,
  output out_4,
  output [7:0] S
);

  wire somador1bit_1_cout, somador1bit_3_cout, somador1bit_4_cout, somador1bit_5_cout, somador1bit_6_cout,
       somador1bit_7_cout;

  somador1bit somador1bit_1 (.A(A[0]), .B(B[0]), .Cin(in_2), .Cout(somador1bit_1_cout), .S(S[0]));
  somador1bit somador1bit_2 (.A(A[1]), .B(B[1]), .Cin(somador1bit_1_cout), .Cout(B[2]), .S(S[1]));
  somador1bit somador1bit_3 (.A(A[2]), .B(B[2]), .Cin(B[2]), .Cout(somador1bit_3_cout), .S(S[2]));
  somador1bit somador1bit_4 (.A(A[3]), .B(B[3]), .Cin(somador1bit_3_cout), .Cout(somador1bit_4_cout), .S(S[3]));
  somador1bit somador1bit_5 (.A(A[4]), .B(B[4]), .Cin(somador1bit_4_cout), .Cout(somador1bit_5_cout), .S(S[4]));
  somador1bit somador1bit_6 (.A(A[5]), .B(B[5]), .Cin(somador1bit_5_cout), .Cout(somador1bit_6_cout), .S(S[5]));
  somador1bit somador1bit_7 (.A(A[6]), .B(B[6]), .Cin(somador1bit_6_cout), .Cout(somador1bit_7_cout), .S(S[6]));
  somador1bit somador1bit_8 (.A(A[7]), .B(B[7]), .Cin(somador1bit_7_cout), .Cout(out_4), .S(S[7]));
endmodule

module Memoria1Bit (
  input  I,
  input  S,
  output Q
);

  wire nand_1_out, nand_2_out, nand_4_out;

  nand nand_1 (nand_1_out, I, S);
  nand nand_2 (nand_2_out, nand_1_out, S);
  nand nand_3 (Q, nand_1_out, nand_4_out);
  nand nand_4 (nand_4_out, Q, nand_2_out);

  // Notes on the sheet:
  //   Input | Set | Output
  //   0   |  0  |  x
  //   1   |  0  |  x
  //   0   |  1  |  0
  //   1   |  1  |  1
  //   (armazenado)
  //   (armazenado)
endmodule

module Memoria8Bits (
  input  in_1,
  input  [7:0] in_2,
  output [7:0] out_3
);

  Memoria1Bit memoria1bit_1 (.S(in_1), .I(in_2[0]), .Q(out_3[0]));
  Memoria1Bit memoria1bit_2 (.S(in_1), .I(in_2[1]), .Q(out_3[1]));
  Memoria1Bit memoria1bit_3 (.S(in_1), .I(in_2[2]), .Q(out_3[2]));
  Memoria1Bit memoria1bit_4 (.S(in_1), .I(in_2[3]), .Q(out_3[3]));
  Memoria1Bit memoria1bit_5 (.S(in_1), .I(in_2[4]), .Q(out_3[4]));
  Memoria1Bit memoria1bit_6 (.S(in_1), .I(in_2[5]), .Q(out_3[5]));
  Memoria1Bit memoria1bit_7 (.S(in_1), .I(in_2[6]), .Q(out_3[6]));
  Memoria1Bit memoria1bit_8 (.S(in_1), .I(in_2[7]), .Q(out_3[7]));
endmodule

module Registrador (
  input  S,
  input  [7:0] I,
  input  E,
  output [7:0] O
);

  wire [7:0] memoria8bits_1_p3;

  // Memoria8Bits memoria8bits_1: pin names not known; wires that end beside it: I, S, memoria8bits_1_p3
  and and_1 (O[0], memoria8bits_1_p3[0], E);
  and and_2 (O[1], memoria8bits_1_p3[1], E);
  and and_3 (O[2], memoria8bits_1_p3[2], E);
  and and_4 (O[3], memoria8bits_1_p3[3], E);
  and and_5 (O[4], memoria8bits_1_p3[4], E);
  and and_6 (O[5], memoria8bits_1_p3[5], E);
  and and_7 (O[6], memoria8bits_1_p3[6], E);
  and and_8 (O[7], memoria8bits_1_p3[7], E);
endmodule

module Memoria1byte (
  input  Set,
  input  [7:0] Inp,
  output out_3,
  output out_4,
  output out_5,
  output out_6,
  output out_7,
  output out_8,
  output out_9,
  output out_10
);

  Memoria1Bit memoria1bit_1 (.S(Set), .I(Inp[0]), .Q(out_3));
  Memoria1Bit memoria1bit_2 (.S(Set), .I(Inp[1]), .Q(out_4));
  Memoria1Bit memoria1bit_3 (.S(Set), .I(Inp[2]), .Q(out_5));
  Memoria1Bit memoria1bit_4 (.S(Set), .I(Inp[3]), .Q(out_6));
  Memoria1Bit memoria1bit_5 (.S(Set), .I(Inp[4]), .Q(out_7));
  Memoria1Bit memoria1bit_6 (.S(Set), .I(Inp[5]), .Q(out_8));
  Memoria1Bit memoria1bit_7 (.S(Set), .I(Inp[6]), .Q(out_9));
  Memoria1Bit memoria1bit_8 (.S(Set), .I(Inp[7]), .Q(out_10));
endmodule

module Controll_buffer (
  input  in_1,
  input  in_2,
  input  in_3,
  input  in_4,
  input  in_5,
  input  [7:0] in_6,
  input  [2:0] in_7,
  output [7:0] out_8
);

  wire undriven, undriven_2, undriven_3;
  wire [7:0] controlled_buffer_1_out, MAR_q, ram_1_data, register_1_q, register_2_q;

  Shifter shifter_1 (.in(in_6), .\dist (in_7), .out(out_8));
  Register register_1 (.D(controlled_buffer_1_out), .Q(register_1_q), .clk(in_4));  // open: en, clr
  assign controlled_buffer_1_out = in_5 ? register_1_q : 8'bz;  // Controlled_Buffer controlled_buffer_1
  Register register_2 (.D(controlled_buffer_1_out), .Q(register_2_q), .clk(in_2));  // open: en, clr
  assign controlled_buffer_1_out = in_3 ? register_2_q : 8'bz;  // Controlled_Buffer controlled_buffer_2
  Register MAR (.D(controlled_buffer_1_out), .Q(MAR_q), .clk(in_1));  // open: en, clr
  RAM #(.databus("bidir")) ram_1 (.addr(MAR_q), .we(undriven), .oe(undriven_2), .clk(undriven_3), .data(ram_1_data));
endmodule

module MEM_RAM (
  input  [7:0] Dado,
  input  in_2,
  input  [7:0] Endereco,
  input  in_4,
  input  in_5,
  output [7:0] out_6
);

  wire and_1_out, and_2_out, and_3_out, and_4_out, and_5_out, and_6_out, and_7_out, and_8_out, and_9_out,
       decoder_1_out0, decoder_1_out1, decoder_1_out2, decoder_2_out0, undriven_3, undriven_4, undriven_5,
       undriven_6, undriven_7, undriven_8;
  wire [7:0] controlled_buffer_7_out, controlled_buffer_8_out, register_1_q, register_2_q, register_3_q,
       register_4_q, register_5_q, register_6_q, register_7_q, undriven, undriven_2;

  Decoder #(.select(4)) decoder_1 (
    .out0(decoder_1_out0), .out1(decoder_1_out1), .out2(decoder_1_out2), .sel(Endereco[3:0]));  // open: out3, out4, out5, out6, out7, out8, out9, out10, out11, out12, out13, out14, out15, en
  Decoder #(.select(4)) decoder_2 (
    .out0(decoder_2_out0), .sel(Endereco[7:4]));  // open: out1, out2, out3, out4, out5, out6, out7, out8, out9, out10, out11, out12, out13, out14, out15, en
  Register register_1 (.D(Dado), .Q(register_1_q), .clk(in_2));  // open: en, clr
  and and_1 (and_1_out, decoder_1_out0, decoder_2_out0);
  Register register_2 (.D(undriven), .Q(register_2_q), .clk(in_4));  // open: en, clr
  and and_2 (and_2_out, undriven_4, decoder_2_out0);
  Register register_3 (.D(undriven_2), .Q(register_3_q), .clk(in_5));  // open: en, clr
  and and_3 (and_3_out, undriven_3, decoder_2_out0);
  assign register_2_q = and_1_out ? register_1_q : 8'bz;  // Controlled_Buffer controlled_buffer_1
  assign register_3_q = and_2_out ? register_2_q : 8'bz;  // Controlled_Buffer controlled_buffer_2
  assign out_6 = and_3_out ? register_3_q : 8'bz;  // Controlled_Buffer controlled_buffer_3
  Register register_4 (.D(Dado), .Q(register_4_q));  // open: en, clk, clr
  and and_4 (and_4_out, decoder_1_out1, decoder_2_out0);
  Register register_5 (.D(undriven), .Q(register_5_q));  // open: en, clk, clr
  and and_5 (and_5_out, undriven_5, decoder_2_out0);
  Register register_6 (.D(undriven_2), .Q(register_6_q));  // open: en, clk, clr
  and and_6 (and_6_out, undriven_6, decoder_2_out0);
  assign register_5_q = and_4_out ? register_4_q : 8'bz;  // Controlled_Buffer controlled_buffer_4
  assign register_6_q = and_5_out ? register_5_q : 8'bz;  // Controlled_Buffer controlled_buffer_5
  assign out_6 = and_6_out ? register_6_q : 8'bz;  // Controlled_Buffer controlled_buffer_6
  and and_7 (and_7_out, decoder_1_out2, decoder_2_out0);
  and and_8 (and_8_out, undriven_7, decoder_2_out0);
  and and_9 (and_9_out, undriven_8, decoder_2_out0);
  Register register_7 (.D(Dado), .Q(register_7_q));  // open: en, clk, clr
  assign controlled_buffer_7_out = and_7_out ? register_7_q : 8'bz;  // Controlled_Buffer controlled_buffer_7
  Register register_8 (.D(undriven), .Q(controlled_buffer_7_out));  // open: en, clk, clr
  assign controlled_buffer_8_out = and_8_out ? controlled_buffer_7_out : 8'bz;  // Controlled_Buffer controlled_buffer_8
  Register register_9 (.D(undriven_2), .Q(controlled_buffer_8_out));  // open: en, clk, clr
  assign out_6 = and_9_out ? controlled_buffer_8_out : 8'bz;  // Controlled_Buffer controlled_buffer_9
endmodule

module ULA (
  input  [2:0] OP,
  input  [7:0] A,
  input  [7:0] B,
  input  Cin,
  output Cout,
  output [7:0] Result,
  output A_Maior,
  output Igual,
  output Zero
);

  wire adder_1_cout, or_2_out, s_left_1_cout, s_right_1_cout;
  wire [7:0] adder_1_out, and_1_out, not_1_out, or_1_out, s_left_1_out_2, s_right_1_out_3, xor_1_out;

  Adder adder_1 (.a(A), .b(B), .out(adder_1_out), .cin(Cin), .cout(adder_1_cout));
  S_Right s_right_1 (.in_1(A), .Cout(s_right_1_cout), .out_3(s_right_1_out_3));
  S_Left s_left_1 (.in_1(A), .out_2(s_left_1_out_2), .Cout(s_left_1_cout));
  assign not_1_out = ~A;  // NOT_Gate not_1, 8 bits wide
  assign and_1_out = A & B;  // AND_Gate and_1, 8 bits wide
  assign or_1_out = A | B;  // OR_Gate or_1, 8 bits wide
  assign xor_1_out = A ^ B;  // XOR_Gate xor_1, 8 bits wide
  Comparator comparator_1 (.a(A), .b(B), .gt(A_Maior), .eq(Igual));  // open: lt
  Multiplexer #(.select(3), .width(8)) multiplexer_1 (
    .in0(adder_1_out), .in1(s_right_1_out_3), .in2(s_left_1_out_2), .in3(not_1_out), .in4(and_1_out),
    .in5(or_1_out), .in6(xor_1_out), .in7(A), .out(Result), .sel(OP));
  Multiplexer #(.select(3)) multiplexer_2 (
    .in0(adder_1_cout), .in1(s_right_1_cout), .in2(s_left_1_cout), .in3(1'b0), .in4(1'b0), .in5(1'b0),
    .in6(1'b0), .in7(1'b0), .out(Cout), .sel(OP));
  or or_2 (or_2_out, Result[0], Result[1], Result[2], Result[3], Result[4], Result[5], Result[6], Result[7]);
  not not_2 (Zero, or_2_out);
endmodule

module S_Left (
  input  [7:0] in_1,
  output [7:0] out_2,
  output Cout
);


  assign Cout = in_1[7];
  assign out_2 = {in_1[6:0], 1'b0};
endmodule

module S_Right (
  input  [7:0] in_1,
  output Cout,
  output [7:0] out_3
);


  assign Cout = in_1[0];
  assign out_3 = {{2{in_1[7]}}, in_1[6:1]};
endmodule

module bus1 (
  input  [7:0] in_1,
  input  in_2,
  output [7:0] out_3
);

  Multiplexer #(.width(8)) multiplexer_1 (.in0(in_1), .in1(8'h1), .out(out_3), .sel(in_2));
endmodule

module clocker (
  output clk_s,
  output out_2,
  output clk_e
);

  wire clk_d_out;

  Clock #(.highDuration(2), .lowDuration(2)) clk (.out(out_2));
  Clock #(.highDuration(2), .lowDuration(2), .phaseOffset(3)) clk_d (.out(clk_d_out));
  and and_1 (clk_s, out_2, clk_d_out);
  or or_1 (clk_e, out_2, clk_d_out);
endmodule

module Stepper (
  input  in_1,
  output init_cycle,
  output out_3,
  output out_4,
  output out_5,
  output out_6,
  output out_7,
  output out_8
);

  wire decoder_1_out7;
  wire [2:0] counter_1_q;

  Counter #(.max('h7), .width(3)) counter_1 (
    .load(1'b0), .Q(counter_1_q), .up(1'b1), .clk(in_1), .clr(decoder_1_out7));  // open: D, count, carry
  Decoder #(.enable("false"), .select(3)) decoder_1 (
    .out0(init_cycle), .out1(out_3), .out2(out_4), .out3(out_5), .out4(out_6), .out5(out_7), .out6(out_8),
    .out7(decoder_1_out7), .sel(counter_1_q));
endmodule

module UC (
);

  wire clocker_1_clk_e, clocker_1_clk_s, clocker_1_out_2;

  clocker clocker_1 (.clk_s(clocker_1_clk_s), .out_2(clocker_1_out_2), .clk_e(clocker_1_clk_e));
  Stepper stepper_1 (.in_1(clocker_1_out_2));  // open: out_3, out_4, out_5, out_6, out_7, out_8, init_cycle
endmodule
